// Digital circuit ADDER_SUBTRACTOR.dig as structural Verilog
module ADDER_SUBTRACTOR (
  input  A7,
  input  A6,
  input  A5,
  input  A4,
  input  A3,
  input  A2,
  input  A1,
  input  A0,
  input  B7,
  input  B6,
  input  B5,
  input  B4,
  input  B3,
  input  B2,
  input  B1,
  input  B0,
  input  ADD_SUB,
  input  in_19,
  output C0,
  output out_20,
  output out_21,
  output out_22,
  output out_23,
  output out_24,
  output out_25,
  output out_26,
  output out_27
);

  wire add_1_s, add_2_c_o, add_2_s, add_3_c_o, add_3_s, add_4_c_o, add_4_s, add_5_c_o, add_5_s, add_6_c_o,
       add_6_s, add_7_c_o, add_7_s, add_8_c_o, add_8_s, xor_1_out, xor_2_out, xor_3_out, xor_4_out,
       xor_5_out, xor_6_out, xor_7_out, xor_8_out;

  Add add_1 (.a(A7), .b(xor_1_out), .c_i(add_2_c_o), .s(add_1_s), .c_o(C0));
  Add add_2 (.a(A6), .b(xor_2_out), .c_i(add_3_c_o), .s(add_2_s), .c_o(add_2_c_o));
  xor xor_1 (xor_1_out, ADD_SUB, B7);
  Add add_3 (.a(A5), .b(xor_3_out), .c_i(add_4_c_o), .s(add_3_s), .c_o(add_3_c_o));
  xor xor_2 (xor_2_out, ADD_SUB, B6);
  xor xor_3 (xor_3_out, ADD_SUB, B5);
  D_FF d_ff_1 (.D(add_1_s), .C(in_19), .Q(out_20));  // open: nQ
  xor xor_4 (xor_4_out, ADD_SUB, B4);
  D_FF d_ff_2 (.D(add_2_s), .C(in_19), .Q(out_21));  // open: nQ
  xor xor_5 (xor_5_out, ADD_SUB, B3);
  Add add_4 (.a(A4), .b(xor_4_out), .c_i(add_5_c_o), .s(add_4_s), .c_o(add_4_c_o));
  D_FF d_ff_3 (.D(add_3_s), .C(in_19), .Q(out_22));  // open: nQ
  xor xor_6 (xor_6_out, ADD_SUB, B2);
  D_FF d_ff_4 (.D(add_5_s), .C(in_19), .Q(out_24));  // open: nQ
  D_FF d_ff_5 (.D(add_4_s), .C(in_19), .Q(out_23));  // open: nQ
  xor xor_7 (xor_7_out, ADD_SUB, B1);
  D_FF d_ff_6 (.D(add_6_s), .C(in_19), .Q(out_25));  // open: nQ
  xor xor_8 (xor_8_out, ADD_SUB, B0);
  Add add_5 (.a(A3), .b(xor_5_out), .c_i(add_6_c_o), .s(add_5_s), .c_o(add_5_c_o));
  D_FF d_ff_7 (.D(add_7_s), .C(in_19), .Q(out_26));  // open: nQ
  D_FF d_ff_8 (.D(add_8_s), .C(in_19), .Q(out_27));  // open: nQ
  Add add_6 (.a(A2), .b(xor_6_out), .c_i(add_7_c_o), .s(add_6_s), .c_o(add_6_c_o));
  Add add_7 (.a(A1), .b(xor_7_out), .c_i(add_8_c_o), .s(add_7_s), .c_o(add_7_c_o));
  Add add_8 (.a(A0), .b(xor_8_out), .c_i(ADD_SUB), .s(add_8_s), .c_o(add_8_c_o));
endmodule
