// Digital circuit ARETHEMATIC_PROCESSING_UNIT.dig as structural Verilog
module ARETHEMATIC_PROCESSING_UNIT (
  input  in_1,
  input  in_2,
  input  in_3,
  input  in_4,
  input  in_5,
  input  in_6,
  input  in_7,
  input  in_9,
  input  in_10,
  input  in_11,
  input  in_12,
  input  in_13,
  input  in_14,
  input  in_15,
  input  in_16,
  input  in_17,
  input  in_18,
  input  in_19,
  output out_8,
  output out_20,
  output out_21,
  output out_22,
  output out_23,
  output out_24,
  output out_25,
  output out_26,
  output out_27
);

  wire add_1_s, add_2_c_o, add_2_s, add_3_c_o, add_3_s, add_4_c_o, add_4_s, add_5_c_o, add_5_s, add_6_c_o,
       add_6_s, add_7_c_o, add_7_s, add_8_c_o, add_8_s, and_1_out, and_2_out, and_3_out, and_4_out,
       and_5_out, and_6_out, and_7_out, and_8_out, and_9_out, and_10_out, and_11_out, and_12_out, and_13_out,
       and_14_out, and_15_out, and_16_out, and_17_out, and_18_out, and_19_out, and_20_out, and_21_out,
       and_22_out, and_23_out, and_24_out, and_25_out, and_26_out, and_27_out, and_28_out, and_29_out,
       and_30_out, and_31_out, and_32_out, and_33_out, and_34_out, and_35_out, and_36_out, and_37_out,
       and_38_out, and_39_out, and_40_out, and_41_out, and_42_out, and_43_out, and_44_out, and_45_out,
       and_46_out, and_47_out, and_48_out, and_49_out, and_50_out, and_51_out, and_52_out, and_53_out,
       and_54_out, and_55_out, and_56_out, and_57_out, and_58_out, and_59_out, and_60_out, and_61_out,
       and_62_out, and_63_out, and_64_out, and_65_out, and_66_out, and_67_out, and_68_out, and_69_out,
       and_70_out, and_71_out, and_72_out, and_73_out, and_74_out, and_75_out, and_76_out, and_77_out,
       and_78_out, and_79_out, and_80_out, d_ff_1_q, d_ff_2_q, d_ff_3_q, d_ff_4_q, d_ff_5_q, d_ff_6_q,
       d_ff_7_q, d_ff_8_q, d_ff_9_q, d_ff_10_q, d_ff_11_q, d_ff_12_q, d_ff_13_q, d_ff_14_q, d_ff_15_q,
       d_ff_16_q, d_ff_17_q, d_ff_18_q, d_ff_19_q, d_ff_20_q, d_ff_21_q, d_ff_22_q, d_ff_23_q, d_ff_24_q,
       d_ff_25_q, d_ff_26_q, d_ff_27_q, d_ff_28_q, d_ff_29_q, d_ff_30_q, d_ff_31_q, d_ff_32_q, d_ff_33_q,
       d_ff_34_q, d_ff_35_q, d_ff_36_q, d_ff_37_q, d_ff_38_q, d_ff_39_q, d_ff_40_q, d_ff_41_q, d_ff_42_q,
       d_ff_43_q, d_ff_44_q, d_ff_45_q, d_ff_46_q, d_ff_47_q, d_ff_48_q, d_ff_49_q, d_ff_50_q, d_ff_51_q,
       d_ff_52_q, d_ff_53_q, d_ff_54_q, d_ff_55_q, d_ff_56_q, d_ff_57_q, d_ff_58_q, d_ff_59_q, d_ff_60_q,
       d_ff_61_q, d_ff_62_q, d_ff_63_q, d_ff_64_q, d_ff_65_q, d_ff_66_q, d_ff_67_q, d_ff_68_q, d_ff_69_q,
       d_ff_70_q, d_ff_71_q, d_ff_72_q, d_ff_73_q, d_ff_74_q, d_ff_75_q, d_ff_76_q, d_ff_77_q, d_ff_78_q,
       d_ff_79_q, d_ff_80_q, not_1_out, not_2_out, not_3_out, not_4_out, not_5_out, not_6_out, not_7_out,
       not_8_out, not_9_out, not_10_out, not_11_out, not_12_out, or_1_out, or_2_out, or_3_out, or_4_out,
       or_5_out, or_6_out, or_7_out, or_8_out, or_9_out, or_10_out, or_11_out, or_12_out, or_13_out,
       or_14_out, or_15_out, or_16_out, or_17_out, or_18_out, or_19_out, or_20_out, or_21_out, or_22_out,
       or_23_out, or_24_out, xor_1_out, xor_2_out, xor_3_out, xor_4_out, xor_5_out, xor_6_out, xor_7_out,
       xor_8_out;

  not not_1 (not_1_out, in_4);
  not not_2 (not_2_out, in_3);
  not not_3 (not_3_out, in_2);
  not not_4 (not_4_out, in_4);
  not not_5 (not_5_out, in_3);
  not not_6 (not_6_out, in_4);
  not not_7 (not_7_out, in_2);
  not not_8 (not_8_out, in_4);
  not not_9 (not_9_out, in_3);
  not not_10 (not_10_out, in_2);
  not not_11 (not_11_out, in_3);
  not not_12 (not_12_out, in_2);
  and and_1 (and_1_out, not_1_out, not_2_out, not_3_out);
  and and_2 (and_2_out, not_4_out, not_5_out, in_2);
  and and_3 (and_3_out, not_6_out, in_3, not_7_out);
  and and_4 (and_4_out, not_8_out, in_3, in_2);
  and and_5 (and_5_out, in_4, not_9_out, not_10_out);
  and and_6 (and_6_out, in_4, not_11_out, in_2);
  and and_7 (and_7_out, in_4, in_3, not_12_out);
  and and_8 (and_8_out, in_4, in_3, in_2);
  and and_9 (and_9_out, in_1, and_1_out);
  and and_10 (and_10_out, in_1, and_2_out);
  and and_11 (and_11_out, in_1, and_3_out);
  and and_12 (and_12_out, in_1, and_4_out);
  and and_13 (and_13_out, in_1, and_5_out);
  and and_14 (and_14_out, in_1, and_6_out);
  and and_15 (and_15_out, in_1, and_7_out);
  and and_16 (and_16_out, in_1, and_8_out);
  D_FF d_ff_1 (.D(out_20), .C(and_9_out), .Q(d_ff_1_q));  // open: nQ
  D_FF d_ff_2 (.D(out_20), .C(and_10_out), .Q(d_ff_2_q));  // open: nQ
  D_FF d_ff_3 (.D(out_20), .C(and_11_out), .Q(d_ff_3_q));  // open: nQ
  D_FF d_ff_4 (.D(out_20), .C(and_12_out), .Q(d_ff_4_q));  // open: nQ
  D_FF d_ff_5 (.D(out_20), .C(and_13_out), .Q(d_ff_5_q));  // open: nQ
  D_FF d_ff_6 (.D(out_20), .C(and_14_out), .Q(d_ff_6_q));  // open: nQ
  D_FF d_ff_7 (.D(out_20), .C(and_15_out), .Q(d_ff_7_q));  // open: nQ
  D_FF d_ff_8 (.D(out_20), .C(and_16_out), .Q(d_ff_8_q));  // open: nQ
  D_FF d_ff_9 (.D(out_22), .C(and_9_out), .Q(d_ff_9_q));  // open: nQ
  D_FF d_ff_10 (.D(out_21), .C(and_9_out), .Q(d_ff_10_q));  // open: nQ
  D_FF d_ff_11 (.D(out_22), .C(and_10_out), .Q(d_ff_11_q));  // open: nQ
  D_FF d_ff_12 (.D(out_21), .C(and_10_out), .Q(d_ff_12_q));  // open: nQ
  D_FF d_ff_13 (.D(out_22), .C(and_11_out), .Q(d_ff_13_q));  // open: nQ
  D_FF d_ff_14 (.D(out_21), .C(and_11_out), .Q(d_ff_14_q));  // open: nQ
  D_FF d_ff_15 (.D(out_22), .C(and_12_out), .Q(d_ff_15_q));  // open: nQ
  D_FF d_ff_16 (.D(out_21), .C(and_12_out), .Q(d_ff_16_q));  // open: nQ
  D_FF d_ff_17 (.D(out_22), .C(and_13_out), .Q(d_ff_17_q));  // open: nQ
  D_FF d_ff_18 (.D(out_21), .C(and_13_out), .Q(d_ff_18_q));  // open: nQ
  D_FF d_ff_19 (.D(out_22), .C(and_14_out), .Q(d_ff_19_q));  // open: nQ
  D_FF d_ff_20 (.D(out_21), .C(and_14_out), .Q(d_ff_20_q));  // open: nQ
  D_FF d_ff_21 (.D(out_22), .C(and_15_out), .Q(d_ff_21_q));  // open: nQ
  D_FF d_ff_22 (.D(out_21), .C(and_15_out), .Q(d_ff_22_q));  // open: nQ
  D_FF d_ff_23 (.D(out_22), .C(and_16_out), .Q(d_ff_23_q));  // open: nQ
  D_FF d_ff_24 (.D(out_21), .C(and_16_out), .Q(d_ff_24_q));  // open: nQ
  D_FF d_ff_25 (.D(out_24), .C(and_9_out), .Q(d_ff_25_q));  // open: nQ
  D_FF d_ff_26 (.D(out_23), .C(and_9_out), .Q(d_ff_26_q));  // open: nQ
  D_FF d_ff_27 (.D(out_24), .C(and_10_out), .Q(d_ff_27_q));  // open: nQ
  D_FF d_ff_28 (.D(out_23), .C(and_10_out), .Q(d_ff_28_q));  // open: nQ
  D_FF d_ff_29 (.D(out_24), .C(and_11_out), .Q(d_ff_29_q));  // open: nQ
  D_FF d_ff_30 (.D(out_23), .C(and_11_out), .Q(d_ff_30_q));  // open: nQ
  D_FF d_ff_31 (.D(out_24), .C(and_12_out), .Q(d_ff_31_q));  // open: nQ
  D_FF d_ff_32 (.D(out_23), .C(and_12_out), .Q(d_ff_32_q));  // open: nQ
  D_FF d_ff_33 (.D(out_24), .C(and_13_out), .Q(d_ff_33_q));  // open: nQ
  D_FF d_ff_34 (.D(out_23), .C(and_13_out), .Q(d_ff_34_q));  // open: nQ
  D_FF d_ff_35 (.D(out_24), .C(and_14_out), .Q(d_ff_35_q));  // open: nQ
  D_FF d_ff_36 (.D(out_23), .C(and_14_out), .Q(d_ff_36_q));  // open: nQ
  D_FF d_ff_37 (.D(out_24), .C(and_15_out), .Q(d_ff_37_q));  // open: nQ
  D_FF d_ff_38 (.D(out_23), .C(and_15_out), .Q(d_ff_38_q));  // open: nQ
  D_FF d_ff_39 (.D(out_24), .C(and_16_out), .Q(d_ff_39_q));  // open: nQ
  D_FF d_ff_40 (.D(out_23), .C(and_16_out), .Q(d_ff_40_q));  // open: nQ
  D_FF d_ff_41 (.D(out_26), .C(and_9_out), .Q(d_ff_41_q));  // open: nQ
  D_FF d_ff_42 (.D(out_25), .C(and_9_out), .Q(d_ff_42_q));  // open: nQ
  D_FF d_ff_43 (.D(out_26), .C(and_10_out), .Q(d_ff_43_q));  // open: nQ
  D_FF d_ff_44 (.D(out_25), .C(and_10_out), .Q(d_ff_44_q));  // open: nQ
  D_FF d_ff_45 (.D(out_26), .C(and_11_out), .Q(d_ff_45_q));  // open: nQ
  D_FF d_ff_46 (.D(out_25), .C(and_11_out), .Q(d_ff_46_q));  // open: nQ
  D_FF d_ff_47 (.D(out_26), .C(and_12_out), .Q(d_ff_47_q));  // open: nQ
  D_FF d_ff_48 (.D(out_25), .C(and_12_out), .Q(d_ff_48_q));  // open: nQ
  D_FF d_ff_49 (.D(out_26), .C(and_13_out), .Q(d_ff_49_q));  // open: nQ
  D_FF d_ff_50 (.D(out_25), .C(and_13_out), .Q(d_ff_50_q));  // open: nQ
  D_FF d_ff_51 (.D(out_26), .C(and_14_out), .Q(d_ff_51_q));  // open: nQ
  D_FF d_ff_52 (.D(out_25), .C(and_14_out), .Q(d_ff_52_q));  // open: nQ
  D_FF d_ff_53 (.D(out_26), .C(and_15_out), .Q(d_ff_53_q));  // open: nQ
  D_FF d_ff_54 (.D(out_25), .C(and_15_out), .Q(d_ff_54_q));  // open: nQ
  D_FF d_ff_55 (.D(out_26), .C(and_16_out), .Q(d_ff_55_q));  // open: nQ
  D_FF d_ff_56 (.D(out_25), .C(and_16_out), .Q(d_ff_56_q));  // open: nQ
  D_FF d_ff_57 (.D(out_27), .C(and_9_out), .Q(d_ff_57_q));  // open: nQ
  D_FF d_ff_58 (.D(out_27), .C(and_10_out), .Q(d_ff_58_q));  // open: nQ
  D_FF d_ff_59 (.D(out_27), .C(and_11_out), .Q(d_ff_59_q));  // open: nQ
  D_FF d_ff_60 (.D(out_27), .C(and_12_out), .Q(d_ff_60_q));  // open: nQ
  D_FF d_ff_61 (.D(out_27), .C(and_13_out), .Q(d_ff_61_q));  // open: nQ
  D_FF d_ff_62 (.D(out_27), .C(and_14_out), .Q(d_ff_62_q));  // open: nQ
  D_FF d_ff_63 (.D(out_27), .C(and_15_out), .Q(d_ff_63_q));  // open: nQ
  D_FF d_ff_64 (.D(out_27), .C(and_16_out), .Q(d_ff_64_q));  // open: nQ
  and and_17 (and_17_out, d_ff_1_q, and_1_out);
  and and_18 (and_18_out, d_ff_10_q, and_1_out);
  and and_19 (and_19_out, d_ff_9_q, and_1_out);
  and and_20 (and_20_out, d_ff_26_q, and_1_out);
  and and_21 (and_21_out, d_ff_25_q, and_1_out);
  and and_22 (and_22_out, d_ff_42_q, and_1_out);
  and and_23 (and_23_out, d_ff_41_q, and_1_out);
  and and_24 (and_24_out, d_ff_57_q, and_1_out);
  and and_25 (and_25_out, d_ff_2_q, and_2_out);
  and and_26 (and_26_out, d_ff_12_q, and_2_out);
  and and_27 (and_27_out, d_ff_11_q, and_2_out);
  and and_28 (and_28_out, d_ff_28_q, and_2_out);
  and and_29 (and_29_out, d_ff_27_q, and_2_out);
  and and_30 (and_30_out, d_ff_44_q, and_2_out);
  and and_31 (and_31_out, d_ff_43_q, and_2_out);
  and and_32 (and_32_out, d_ff_58_q, and_2_out);
  and and_33 (and_33_out, d_ff_3_q, and_3_out);
  and and_34 (and_34_out, d_ff_14_q, and_3_out);
  and and_35 (and_35_out, d_ff_13_q, and_3_out);
  and and_36 (and_36_out, d_ff_30_q, and_3_out);
  and and_37 (and_37_out, d_ff_29_q, and_3_out);
  and and_38 (and_38_out, d_ff_46_q, and_3_out);
  and and_39 (and_39_out, d_ff_45_q, and_3_out);
  and and_40 (and_40_out, d_ff_59_q, and_3_out);
  and and_41 (and_41_out, d_ff_4_q, and_4_out);
  and and_42 (and_42_out, d_ff_16_q, and_4_out);
  and and_43 (and_43_out, d_ff_15_q, and_4_out);
  and and_44 (and_44_out, d_ff_32_q, and_4_out);
  and and_45 (and_45_out, d_ff_31_q, and_4_out);
  and and_46 (and_46_out, d_ff_48_q, and_4_out);
  and and_47 (and_47_out, d_ff_47_q, and_4_out);
  and and_48 (and_48_out, d_ff_60_q, and_4_out);
  and and_49 (and_49_out, d_ff_5_q, and_5_out);
  and and_50 (and_50_out, d_ff_18_q, and_5_out);
  and and_51 (and_51_out, d_ff_17_q, and_5_out);
  and and_52 (and_52_out, d_ff_34_q, and_5_out);
  and and_53 (and_53_out, d_ff_33_q, and_5_out);
  and and_54 (and_54_out, d_ff_50_q, and_5_out);
  and and_55 (and_55_out, d_ff_49_q, and_5_out);
  and and_56 (and_56_out, d_ff_61_q, and_5_out);
  and and_57 (and_57_out, d_ff_6_q, and_6_out);
  and and_58 (and_58_out, d_ff_20_q, and_6_out);
  and and_59 (and_59_out, d_ff_19_q, and_6_out);
  and and_60 (and_60_out, d_ff_36_q, and_6_out);
  and and_61 (and_61_out, d_ff_35_q, and_6_out);
  and and_62 (and_62_out, d_ff_52_q, and_6_out);
  and and_63 (and_63_out, d_ff_51_q, and_6_out);
  and and_64 (and_64_out, d_ff_62_q, and_6_out);
  and and_65 (and_65_out, d_ff_7_q, and_7_out);
  and and_66 (and_66_out, d_ff_22_q, and_7_out);
  and and_67 (and_67_out, d_ff_21_q, and_7_out);
  and and_68 (and_68_out, d_ff_38_q, and_7_out);
  and and_69 (and_69_out, d_ff_37_q, and_7_out);
  and and_70 (and_70_out, d_ff_54_q, and_7_out);
  and and_71 (and_71_out, d_ff_53_q, and_7_out);
  and and_72 (and_72_out, d_ff_63_q, and_7_out);
  and and_73 (and_73_out, d_ff_8_q, and_8_out);
  and and_74 (and_74_out, d_ff_24_q, and_8_out);
  and and_75 (and_75_out, d_ff_23_q, and_8_out);
  and and_76 (and_76_out, d_ff_40_q, and_8_out);
  and and_77 (and_77_out, d_ff_39_q, and_8_out);
  and and_78 (and_78_out, d_ff_56_q, and_8_out);
  and and_79 (and_79_out, d_ff_55_q, and_8_out);
  and and_80 (and_80_out, d_ff_64_q, and_8_out);
  or or_1 (or_1_out, and_49_out, and_57_out, and_65_out, and_73_out);
  or or_2 (or_2_out, and_50_out, and_58_out, and_66_out, and_74_out);
  or or_3 (or_3_out, and_51_out, and_59_out, and_67_out, and_75_out);
  or or_4 (or_4_out, and_44_out, and_52_out, and_68_out, and_76_out);
  or or_5 (or_5_out, and_45_out, and_53_out, and_61_out, and_77_out);
  or or_6 (or_6_out, and_54_out, and_62_out, and_70_out, and_78_out);
  or or_7 (or_7_out, and_25_out, and_33_out, and_41_out, or_1_out);
  or or_8 (or_8_out, and_26_out, and_34_out, and_42_out, or_2_out);
  or or_9 (or_9_out, and_27_out, and_35_out, and_43_out, or_3_out);
  or or_10 (or_10_out, and_60_out, and_28_out, and_36_out, or_4_out);
  or or_11 (or_11_out, and_55_out, and_63_out, and_71_out, and_79_out);
  or or_12 (or_12_out, and_56_out, and_64_out, and_72_out, and_80_out);
  or or_13 (or_13_out, and_17_out, or_7_out);
  or or_14 (or_14_out, and_18_out, or_8_out);
  or or_15 (or_15_out, and_19_out, or_9_out);
  or or_16 (or_16_out, and_20_out, or_10_out);
  or or_17 (or_17_out, and_69_out, and_29_out, and_37_out, or_5_out);
  or or_18 (or_18_out, and_30_out, and_38_out, and_46_out, or_6_out);
  or or_19 (or_19_out, and_31_out, and_39_out, and_47_out, or_11_out);
  or or_20 (or_20_out, and_32_out, and_40_out, and_48_out, or_12_out);
  or or_21 (or_21_out, and_21_out, or_17_out);
  or or_22 (or_22_out, and_22_out, or_18_out);
  or or_23 (or_23_out, and_23_out, or_19_out);
  or or_24 (or_24_out, and_24_out, or_20_out);
  assign out_20 = in_6 ? or_13_out : 1'bz;  // Driver driver_1
  assign out_21 = in_6 ? or_14_out : 1'bz;  // Driver driver_2
  assign out_22 = in_6 ? or_15_out : 1'bz;  // Driver driver_3
  assign out_23 = in_6 ? or_16_out : 1'bz;  // Driver driver_4
  assign out_24 = in_6 ? or_21_out : 1'bz;  // Driver driver_5
  assign out_25 = in_6 ? or_22_out : 1'bz;  // Driver driver_6
  assign out_26 = in_6 ? or_23_out : 1'bz;  // Driver driver_7
  assign out_27 = in_6 ? or_24_out : 1'bz;  // Driver driver_8
  assign out_20 = in_5 ? in_12 : 1'bz;  // Driver driver_9
  assign out_21 = in_5 ? in_13 : 1'bz;  // Driver driver_10
  assign out_22 = in_5 ? in_14 : 1'bz;  // Driver driver_11
  assign out_23 = in_5 ? in_15 : 1'bz;  // Driver driver_12
  assign out_24 = in_5 ? in_16 : 1'bz;  // Driver driver_13
  assign out_25 = in_5 ? in_17 : 1'bz;  // Driver driver_14
  assign out_26 = in_5 ? in_18 : 1'bz;  // Driver driver_15
  assign out_27 = in_5 ? in_19 : 1'bz;  // Driver driver_16
  assign out_20 = in_7 ? add_1_s : 1'bz;  // Driver driver_17
  assign out_21 = in_7 ? add_2_s : 1'bz;  // Driver driver_18
  assign out_22 = in_7 ? add_3_s : 1'bz;  // Driver driver_19
  assign out_23 = in_7 ? add_4_s : 1'bz;  // Driver driver_20
  assign out_24 = in_7 ? add_5_s : 1'bz;  // Driver driver_21
  assign out_25 = in_7 ? add_6_s : 1'bz;  // Driver driver_22
  assign out_26 = in_7 ? add_7_s : 1'bz;  // Driver driver_23
  assign out_27 = in_7 ? add_8_s : 1'bz;  // Driver driver_24
  D_FF d_ff_65 (.D(out_20), .C(in_9), .Q(d_ff_65_q));  // open: nQ
  Add add_1 (.a(d_ff_65_q), .b(xor_1_out), .c_i(add_2_c_o), .s(add_1_s), .c_o(out_8));
  D_FF d_ff_66 (.D(out_21), .C(in_9), .Q(d_ff_66_q));  // open: nQ
  D_FF d_ff_67 (.D(out_22), .C(in_9), .Q(d_ff_67_q));  // open: nQ
  D_FF d_ff_68 (.D(out_23), .C(in_9), .Q(d_ff_68_q));  // open: nQ
  D_FF d_ff_69 (.D(out_24), .C(in_9), .Q(d_ff_69_q));  // open: nQ
  D_FF d_ff_70 (.D(out_25), .C(in_9), .Q(d_ff_70_q));  // open: nQ
  D_FF d_ff_71 (.D(out_26), .C(in_9), .Q(d_ff_71_q));  // open: nQ
  D_FF d_ff_72 (.D(out_27), .C(in_9), .Q(d_ff_72_q));  // open: nQ
  Add add_2 (.a(d_ff_66_q), .b(xor_2_out), .c_i(add_3_c_o), .s(add_2_s), .c_o(add_2_c_o));
  D_FF d_ff_73 (.D(out_20), .C(in_10), .Q(d_ff_73_q));  // open: nQ
  D_FF d_ff_74 (.D(out_21), .C(in_10), .Q(d_ff_74_q));  // open: nQ
  xor xor_1 (xor_1_out, in_11, d_ff_73_q);
  Add add_3 (.a(d_ff_67_q), .b(xor_3_out), .c_i(add_4_c_o), .s(add_3_s), .c_o(add_3_c_o));
  D_FF d_ff_75 (.D(out_22), .C(in_10), .Q(d_ff_75_q));  // open: nQ
  D_FF d_ff_76 (.D(out_23), .C(in_10), .Q(d_ff_76_q));  // open: nQ
  xor xor_2 (xor_2_out, in_11, d_ff_74_q);
  D_FF d_ff_77 (.D(out_24), .C(in_10), .Q(d_ff_77_q));  // open: nQ
  D_FF d_ff_78 (.D(out_25), .C(in_10), .Q(d_ff_78_q));  // open: nQ
  xor xor_3 (xor_3_out, in_11, d_ff_75_q);
  D_FF d_ff_79 (.D(out_26), .C(in_10), .Q(d_ff_79_q));  // open: nQ
  D_FF d_ff_80 (.D(out_27), .C(in_10), .Q(d_ff_80_q));  // open: nQ
  xor xor_4 (xor_4_out, in_11, d_ff_76_q);
  xor xor_5 (xor_5_out, in_11, d_ff_77_q);
  Add add_4 (.a(d_ff_68_q), .b(xor_4_out), .c_i(add_5_c_o), .s(add_4_s), .c_o(add_4_c_o));
  xor xor_6 (xor_6_out, in_11, d_ff_78_q);
  xor xor_7 (xor_7_out, in_11, d_ff_79_q);
  xor xor_8 (xor_8_out, in_11, d_ff_80_q);
  Add add_5 (.a(d_ff_69_q), .b(xor_5_out), .c_i(add_6_c_o), .s(add_5_s), .c_o(add_5_c_o));
  Add add_6 (.a(d_ff_70_q), .b(xor_6_out), .c_i(add_7_c_o), .s(add_6_s), .c_o(add_6_c_o));
  Add add_7 (.a(d_ff_71_q), .b(xor_7_out), .c_i(add_8_c_o), .s(add_7_s), .c_o(add_7_c_o));
  Add add_8 (.a(d_ff_72_q), .b(xor_8_out), .c_i(in_11), .s(add_8_s), .c_o(add_8_c_o));

  // Notes on the sheet:
  //   3X8 DECODER
  //   R0
  //   R1
  //   R2
  //   R3
  //   R4
  //   R5
  //   R6
  //   R7
  //   BUILT BY
  //   @PINARX
  //        	SUJAN ANGADI
  //   64 BIT RAM
  //   MEMORY UNIT
  //   REG ADDRESS SEL 2
  //   REG ADDRESS SEL 1
  //   REG ADDRESS SEL 0
  //   WRITE INTO RAM
  //   ENB SWITCH
  //   DATA INPUT
  //   DATA OUT
  //   8 BIT CONTROLL BUS UNIT
  //   WRITE TO REG A
  //   WRITE TO REG B
  //   ADD/SUB ENB
  //   ARETHEMATIC LOGICAL UNIT
endmodule
