// Digital circuit COUNTER.dig as structural Verilog
module COUNTER (
  input  B7,
  input  B6,
  input  B5,
  input  B4,
  input  B3,
  input  B2,
  input  B1,
  input  B0,
  input  UP_DOWN,
  input  in_11,
  output C0,
  output out_12,
  output out_13,
  output out_14,
  output out_15,
  output out_16,
  output out_17,
  output out_18,
  output out_19
);

  wire add_1_s, add_2_c_o, add_2_s, add_3_c_o, add_3_s, add_4_c_o, add_4_s, add_5_c_o, add_5_s, add_6_c_o,
       add_6_s, add_7_c_o, add_7_s, add_8_c_o, add_8_s, xor_1_out, xor_2_out, xor_3_out, xor_4_out,
       xor_5_out, xor_6_out, xor_7_out, xor_8_out;

  Add add_1 (.a(out_19), .b(xor_1_out), .c_i(add_2_c_o), .s(add_1_s), .c_o(C0));
  Add add_2 (.a(out_18), .b(xor_2_out), .c_i(add_3_c_o), .s(add_2_s), .c_o(add_2_c_o));
  xor xor_1 (xor_1_out, UP_DOWN, B7);
  Add add_3 (.a(out_17), .b(xor_3_out), .c_i(add_4_c_o), .s(add_3_s), .c_o(add_3_c_o));
  xor xor_2 (xor_2_out, UP_DOWN, B6);
  xor xor_3 (xor_3_out, UP_DOWN, B5);
  D_FF d_ff_1 (.D(add_1_s), .C(in_11), .Q(out_19));  // open: nQ
  xor xor_4 (xor_4_out, UP_DOWN, B4);
  D_FF d_ff_2 (.D(add_2_s), .C(in_11), .Q(out_18));  // open: nQ
  xor xor_5 (xor_5_out, UP_DOWN, B3);
  Add add_4 (.a(out_16), .b(xor_4_out), .c_i(add_5_c_o), .s(add_4_s), .c_o(add_4_c_o));
  D_FF d_ff_3 (.D(add_3_s), .C(in_11), .Q(out_17));  // open: nQ
  xor xor_6 (xor_6_out, UP_DOWN, B2);
  D_FF d_ff_4 (.D(add_5_s), .C(in_11), .Q(out_15));  // open: nQ
  D_FF d_ff_5 (.D(add_4_s), .C(in_11), .Q(out_16));  // open: nQ
  xor xor_7 (xor_7_out, UP_DOWN, B1);
  D_FF d_ff_6 (.D(add_6_s), .C(in_11), .Q(out_14));  // open: nQ
  xor xor_8 (xor_8_out, UP_DOWN, B0);
  Add add_5 (.a(out_15), .b(xor_5_out), .c_i(add_6_c_o), .s(add_5_s), .c_o(add_5_c_o));
  D_FF d_ff_7 (.D(add_7_s), .C(in_11), .Q(out_13));  // open: nQ
  D_FF d_ff_8 (.D(add_8_s), .C(in_11), .Q(out_12));  // open: nQ
  Add add_6 (.a(out_14), .b(xor_6_out), .c_i(add_7_c_o), .s(add_6_s), .c_o(add_6_c_o));
  Add add_7 (.a(out_13), .b(xor_7_out), .c_i(add_8_c_o), .s(add_7_s), .c_o(add_7_c_o));
  Add add_8 (.a(out_12), .b(xor_8_out), .c_i(UP_DOWN), .s(add_8_s), .c_o(add_8_c_o));
endmodule
