// Digital circuit D_FLIPFLOP.dig as structural Verilog
module D_FLIPFLOP (
  input  A,
  input  C,
  output Y
);

  wire multiplexer_1_out, not_1_out;

  Multiplexer multiplexer_1 (.sel(C), .in_0(multiplexer_1_out), .in_1(A), .out(multiplexer_1_out));
  Multiplexer multiplexer_2 (.sel(not_1_out), .in_0(Y), .in_1(multiplexer_1_out), .out(Y));
  not not_1 (not_1_out, C);
endmodule
