// Digital circuit READ_WRITE_REGISTER_64BIT.dig as structural Verilog
module READ_WRITE_REGISTER_64BIT (
  input  in_1,
  input  in_2,
  input  in_3,
  input  in_4,
  input  in_5,
  input  in_6,
  input  in_7,
  input  in_8,
  input  in_9,
  input  in_10,
  input  in_11,
  input  in_12,
  output out_13,
  output out_14,
  output out_15,
  output out_16,
  output out_17,
  output out_18,
  output out_19,
  output out_20
);

  wire and_1_out, and_2_out, and_3_out, and_4_out, and_5_out, and_6_out, and_7_out, and_8_out, and_9_out,
       and_10_out, and_11_out, and_12_out, and_13_out, and_14_out, and_15_out, and_16_out, and_17_out,
       and_18_out, and_19_out, and_20_out, and_21_out, and_22_out, and_23_out, and_24_out, and_25_out,
       and_26_out, and_27_out, and_28_out, and_29_out, and_30_out, and_31_out, and_32_out, and_33_out,
       and_34_out, and_35_out, and_36_out, and_37_out, and_38_out, and_39_out, and_40_out, and_41_out,
       and_42_out, and_43_out, and_44_out, and_45_out, and_46_out, and_47_out, and_48_out, and_49_out,
       and_50_out, and_51_out, and_52_out, and_53_out, and_54_out, and_55_out, and_56_out, and_57_out,
       and_58_out, and_59_out, and_60_out, and_61_out, and_62_out, and_63_out, and_64_out, and_65_out,
       and_66_out, and_67_out, and_68_out, and_69_out, and_70_out, and_71_out, and_72_out, and_73_out,
       and_74_out, and_75_out, and_76_out, and_77_out, and_78_out, and_79_out, and_80_out, d_ff_1_q,
       d_ff_2_q, d_ff_3_q, d_ff_4_q, d_ff_5_q, d_ff_6_q, d_ff_7_q, d_ff_8_q, d_ff_9_q, d_ff_10_q, d_ff_11_q,
       d_ff_12_q, d_ff_13_q, d_ff_14_q, d_ff_15_q, d_ff_16_q, d_ff_17_q, d_ff_18_q, d_ff_19_q, d_ff_20_q,
       d_ff_21_q, d_ff_22_q, d_ff_23_q, d_ff_24_q, d_ff_25_q, d_ff_26_q, d_ff_27_q, d_ff_28_q, d_ff_29_q,
       d_ff_30_q, d_ff_31_q, d_ff_32_q, d_ff_33_q, d_ff_34_q, d_ff_35_q, d_ff_36_q, d_ff_37_q, d_ff_38_q,
       d_ff_39_q, d_ff_40_q, d_ff_41_q, d_ff_42_q, d_ff_43_q, d_ff_44_q, d_ff_45_q, d_ff_46_q, d_ff_47_q,
       d_ff_48_q, d_ff_49_q, d_ff_50_q, d_ff_51_q, d_ff_52_q, d_ff_53_q, d_ff_54_q, d_ff_55_q, d_ff_56_q,
       d_ff_57_q, d_ff_58_q, d_ff_59_q, d_ff_60_q, d_ff_61_q, d_ff_62_q, d_ff_63_q, d_ff_64_q, not_1_out,
       not_2_out, not_3_out, not_4_out, not_5_out, not_6_out, not_7_out, not_8_out, not_9_out, not_10_out,
       not_11_out, not_12_out, or_1_out, or_2_out, or_3_out, or_4_out, or_5_out, or_6_out, or_7_out,
       or_8_out, or_9_out, or_10_out, or_11_out, or_12_out, or_13_out, or_18_out, or_19_out, or_20_out;

  and and_1 (and_1_out, not_1_out, not_2_out, not_3_out);
  not not_1 (not_1_out, in_1);
  not not_2 (not_2_out, in_2);
  not not_3 (not_3_out, in_3);
  and and_2 (and_2_out, not_4_out, not_5_out, in_3);
  not not_4 (not_4_out, in_1);
  not not_5 (not_5_out, in_2);
  and and_3 (and_3_out, not_6_out, in_2, not_7_out);
  not not_6 (not_6_out, in_1);
  not not_7 (not_7_out, in_3);
  and and_4 (and_4_out, not_8_out, in_2, in_3);
  not not_8 (not_8_out, in_1);
  and and_5 (and_5_out, in_1, not_9_out, not_10_out);
  not not_9 (not_9_out, in_2);
  not not_10 (not_10_out, in_3);
  and and_6 (and_6_out, in_1, not_11_out, in_3);
  not not_11 (not_11_out, in_2);
  and and_7 (and_7_out, in_1, in_2, not_12_out);
  not not_12 (not_12_out, in_3);
  and and_8 (and_8_out, in_1, in_2, in_3);
  and and_9 (and_9_out, in_4, and_1_out);
  and and_10 (and_10_out, in_4, and_2_out);
  and and_11 (and_11_out, in_4, and_3_out);
  and and_12 (and_12_out, in_4, and_4_out);
  and and_13 (and_13_out, in_4, and_5_out);
  and and_14 (and_14_out, in_4, and_6_out);
  and and_15 (and_15_out, in_4, and_7_out);
  and and_16 (and_16_out, in_4, and_8_out);
  D_FF d_ff_1 (.D(in_6), .C(and_9_out), .Q(d_ff_1_q));  // open: nQ
  D_FF d_ff_2 (.D(in_5), .C(and_9_out), .Q(d_ff_2_q));  // open: nQ
  D_FF d_ff_3 (.D(in_6), .C(and_10_out), .Q(d_ff_3_q));  // open: nQ
  D_FF d_ff_4 (.D(in_5), .C(and_10_out), .Q(d_ff_4_q));  // open: nQ
  D_FF d_ff_5 (.D(in_5), .C(and_11_out), .Q(d_ff_5_q));  // open: nQ
  D_FF d_ff_6 (.D(in_5), .C(and_12_out), .Q(d_ff_6_q));  // open: nQ
  D_FF d_ff_7 (.D(in_5), .C(and_13_out), .Q(d_ff_7_q));  // open: nQ
  D_FF d_ff_8 (.D(in_5), .C(and_14_out), .Q(d_ff_8_q));  // open: nQ
  D_FF d_ff_9 (.D(in_5), .C(and_15_out), .Q(d_ff_9_q));  // open: nQ
  D_FF d_ff_10 (.D(in_5), .C(and_16_out), .Q(d_ff_10_q));  // open: nQ
  D_FF d_ff_11 (.D(in_8), .C(and_9_out), .Q(d_ff_11_q));  // open: nQ
  D_FF d_ff_12 (.D(in_7), .C(and_9_out), .Q(d_ff_12_q));  // open: nQ
  D_FF d_ff_13 (.D(in_8), .C(and_10_out), .Q(d_ff_13_q));  // open: nQ
  D_FF d_ff_14 (.D(in_7), .C(and_10_out), .Q(d_ff_14_q));  // open: nQ
  D_FF d_ff_15 (.D(in_7), .C(and_11_out), .Q(d_ff_15_q));  // open: nQ
  D_FF d_ff_16 (.D(in_6), .C(and_11_out), .Q(d_ff_16_q));  // open: nQ
  D_FF d_ff_17 (.D(in_7), .C(and_12_out), .Q(d_ff_17_q));  // open: nQ
  D_FF d_ff_18 (.D(in_6), .C(and_12_out), .Q(d_ff_18_q));  // open: nQ
  D_FF d_ff_19 (.D(in_7), .C(and_13_out), .Q(d_ff_19_q));  // open: nQ
  D_FF d_ff_20 (.D(in_6), .C(and_13_out), .Q(d_ff_20_q));  // open: nQ
  D_FF d_ff_21 (.D(in_7), .C(and_14_out), .Q(d_ff_21_q));  // open: nQ
  D_FF d_ff_22 (.D(in_6), .C(and_14_out), .Q(d_ff_22_q));  // open: nQ
  D_FF d_ff_23 (.D(in_7), .C(and_15_out), .Q(d_ff_23_q));  // open: nQ
  D_FF d_ff_24 (.D(in_6), .C(and_15_out), .Q(d_ff_24_q));  // open: nQ
  D_FF d_ff_25 (.D(in_7), .C(and_16_out), .Q(d_ff_25_q));  // open: nQ
  D_FF d_ff_26 (.D(in_6), .C(and_16_out), .Q(d_ff_26_q));  // open: nQ
  D_FF d_ff_27 (.D(in_10), .C(and_9_out), .Q(d_ff_27_q));  // open: nQ
  D_FF d_ff_28 (.D(in_9), .C(and_9_out), .Q(d_ff_28_q));  // open: nQ
  D_FF d_ff_29 (.D(in_10), .C(and_10_out), .Q(d_ff_29_q));  // open: nQ
  D_FF d_ff_30 (.D(in_9), .C(and_10_out), .Q(d_ff_30_q));  // open: nQ
  D_FF d_ff_31 (.D(in_9), .C(and_11_out), .Q(d_ff_31_q));  // open: nQ
  D_FF d_ff_32 (.D(in_8), .C(and_11_out), .Q(d_ff_32_q));  // open: nQ
  D_FF d_ff_33 (.D(in_9), .C(and_12_out), .Q(d_ff_33_q));  // open: nQ
  D_FF d_ff_34 (.D(in_8), .C(and_12_out), .Q(d_ff_34_q));  // open: nQ
  D_FF d_ff_35 (.D(in_9), .C(and_13_out), .Q(d_ff_35_q));  // open: nQ
  D_FF d_ff_36 (.D(in_8), .C(and_13_out), .Q(d_ff_36_q));  // open: nQ
  D_FF d_ff_37 (.D(in_9), .C(and_14_out), .Q(d_ff_37_q));  // open: nQ
  D_FF d_ff_38 (.D(in_8), .C(and_14_out), .Q(d_ff_38_q));  // open: nQ
  D_FF d_ff_39 (.D(in_9), .C(and_15_out), .Q(d_ff_39_q));  // open: nQ
  D_FF d_ff_40 (.D(in_8), .C(and_15_out), .Q(d_ff_40_q));  // open: nQ
  D_FF d_ff_41 (.D(in_9), .C(and_16_out), .Q(d_ff_41_q));  // open: nQ
  D_FF d_ff_42 (.D(in_8), .C(and_16_out), .Q(d_ff_42_q));  // open: nQ
  D_FF d_ff_43 (.D(in_12), .C(and_9_out), .Q(d_ff_43_q));  // open: nQ
  D_FF d_ff_44 (.D(in_11), .C(and_9_out), .Q(d_ff_44_q));  // open: nQ
  D_FF d_ff_45 (.D(in_12), .C(and_10_out), .Q(d_ff_45_q));  // open: nQ
  D_FF d_ff_46 (.D(in_11), .C(and_10_out), .Q(d_ff_46_q));  // open: nQ
  D_FF d_ff_47 (.D(in_11), .C(and_11_out), .Q(d_ff_47_q));  // open: nQ
  D_FF d_ff_48 (.D(in_10), .C(and_11_out), .Q(d_ff_48_q));  // open: nQ
  D_FF d_ff_49 (.D(in_11), .C(and_12_out), .Q(d_ff_49_q));  // open: nQ
  D_FF d_ff_50 (.D(in_10), .C(and_12_out), .Q(d_ff_50_q));  // open: nQ
  D_FF d_ff_51 (.D(in_11), .C(and_13_out), .Q(d_ff_51_q));  // open: nQ
  D_FF d_ff_52 (.D(in_10), .C(and_13_out), .Q(d_ff_52_q));  // open: nQ
  D_FF d_ff_53 (.D(in_11), .C(and_14_out), .Q(d_ff_53_q));  // open: nQ
  D_FF d_ff_54 (.D(in_10), .C(and_14_out), .Q(d_ff_54_q));  // open: nQ
  D_FF d_ff_55 (.D(in_11), .C(and_15_out), .Q(d_ff_55_q));  // open: nQ
  D_FF d_ff_56 (.D(in_10), .C(and_15_out), .Q(d_ff_56_q));  // open: nQ
  D_FF d_ff_57 (.D(in_11), .C(and_16_out), .Q(d_ff_57_q));  // open: nQ
  D_FF d_ff_58 (.D(in_10), .C(and_16_out), .Q(d_ff_58_q));  // open: nQ
  D_FF d_ff_59 (.D(in_12), .C(and_11_out), .Q(d_ff_59_q));  // open: nQ
  D_FF d_ff_60 (.D(in_12), .C(and_12_out), .Q(d_ff_60_q));  // open: nQ
  D_FF d_ff_61 (.D(in_12), .C(and_13_out), .Q(d_ff_61_q));  // open: nQ
  D_FF d_ff_62 (.D(in_12), .C(and_14_out), .Q(d_ff_62_q));  // open: nQ
  D_FF d_ff_63 (.D(in_12), .C(and_15_out), .Q(d_ff_63_q));  // open: nQ
  D_FF d_ff_64 (.D(in_12), .C(and_16_out), .Q(d_ff_64_q));  // open: nQ
  and and_17 (and_17_out, d_ff_2_q, and_1_out);
  and and_18 (and_18_out, d_ff_1_q, and_1_out);
  and and_19 (and_19_out, d_ff_12_q, and_1_out);
  and and_20 (and_20_out, d_ff_11_q, and_1_out);
  and and_21 (and_21_out, d_ff_28_q, and_1_out);
  and and_22 (and_22_out, d_ff_27_q, and_1_out);
  and and_23 (and_23_out, d_ff_44_q, and_1_out);
  and and_24 (and_24_out, d_ff_43_q, and_1_out);
  and and_25 (and_25_out, d_ff_4_q, and_2_out);
  and and_26 (and_26_out, d_ff_3_q, and_2_out);
  and and_27 (and_27_out, d_ff_14_q, and_2_out);
  and and_28 (and_28_out, d_ff_13_q, and_2_out);
  and and_29 (and_29_out, d_ff_30_q, and_2_out);
  and and_30 (and_30_out, d_ff_29_q, and_2_out);
  and and_31 (and_31_out, d_ff_46_q, and_2_out);
  and and_32 (and_32_out, d_ff_45_q, and_2_out);
  and and_33 (and_33_out, d_ff_5_q, and_3_out);
  and and_34 (and_34_out, d_ff_16_q, and_3_out);
  and and_35 (and_35_out, d_ff_15_q, and_3_out);
  and and_36 (and_36_out, d_ff_32_q, and_3_out);
  and and_37 (and_37_out, d_ff_31_q, and_3_out);
  and and_38 (and_38_out, d_ff_48_q, and_3_out);
  and and_39 (and_39_out, d_ff_47_q, and_3_out);
  and and_40 (and_40_out, d_ff_59_q, and_3_out);
  and and_41 (and_41_out, d_ff_6_q, and_4_out);
  and and_42 (and_42_out, d_ff_18_q, and_4_out);
  and and_43 (and_43_out, d_ff_17_q, and_4_out);
  and and_44 (and_44_out, d_ff_34_q, and_4_out);
  and and_45 (and_45_out, d_ff_33_q, and_4_out);
  and and_46 (and_46_out, d_ff_50_q, and_4_out);
  and and_47 (and_47_out, d_ff_49_q, and_4_out);
  and and_48 (and_48_out, d_ff_60_q, and_4_out);
  and and_49 (and_49_out, d_ff_7_q, and_5_out);
  and and_50 (and_50_out, d_ff_20_q, and_5_out);
  and and_51 (and_51_out, d_ff_19_q, and_5_out);
  and and_52 (and_52_out, d_ff_36_q, and_5_out);
  and and_53 (and_53_out, d_ff_35_q, and_5_out);
  and and_54 (and_54_out, d_ff_52_q, and_5_out);
  and and_55 (and_55_out, d_ff_51_q, and_5_out);
  and and_56 (and_56_out, d_ff_61_q, and_5_out);
  and and_57 (and_57_out, d_ff_8_q, and_6_out);
  and and_58 (and_58_out, d_ff_22_q, and_6_out);
  and and_59 (and_59_out, d_ff_21_q, and_6_out);
  and and_60 (and_60_out, d_ff_38_q, and_6_out);
  and and_61 (and_61_out, d_ff_37_q, and_6_out);
  and and_62 (and_62_out, d_ff_54_q, and_6_out);
  and and_63 (and_63_out, d_ff_53_q, and_6_out);
  and and_64 (and_64_out, d_ff_62_q, and_6_out);
  and and_65 (and_65_out, d_ff_9_q, and_7_out);
  and and_66 (and_66_out, d_ff_24_q, and_7_out);
  and and_67 (and_67_out, d_ff_23_q, and_7_out);
  and and_68 (and_68_out, d_ff_40_q, and_7_out);
  and and_69 (and_69_out, d_ff_39_q, and_7_out);
  and and_70 (and_70_out, d_ff_56_q, and_7_out);
  and and_71 (and_71_out, d_ff_55_q, and_7_out);
  and and_72 (and_72_out, d_ff_63_q, and_7_out);
  and and_73 (and_73_out, d_ff_10_q, and_8_out);
  and and_74 (and_74_out, d_ff_26_q, and_8_out);
  and and_75 (and_75_out, d_ff_25_q, and_8_out);
  and and_76 (and_76_out, d_ff_42_q, and_8_out);
  and and_77 (and_77_out, d_ff_41_q, and_8_out);
  and and_78 (and_78_out, d_ff_58_q, and_8_out);
  and and_79 (and_79_out, d_ff_57_q, and_8_out);
  and and_80 (and_80_out, d_ff_64_q, and_8_out);
  or or_1 (or_1_out, and_49_out, and_57_out, and_65_out, and_73_out);
  or or_2 (or_2_out, and_50_out, and_58_out, and_66_out, and_74_out);
  or or_3 (or_3_out, and_51_out, and_59_out, and_67_out, and_75_out);
  or or_4 (or_4_out, and_44_out, and_52_out, and_68_out, and_76_out);
  or or_5 (or_5_out, and_25_out, and_33_out, and_41_out, or_1_out);
  or or_6 (or_6_out, and_45_out, and_53_out, and_61_out, and_77_out);
  or or_7 (or_7_out, and_54_out, and_62_out, and_70_out, and_78_out);
  or or_8 (or_8_out, and_55_out, and_63_out, and_71_out, and_79_out);
  or or_9 (or_9_out, and_26_out, and_34_out, and_42_out, or_2_out);
  or or_10 (or_10_out, and_27_out, and_35_out, and_43_out, or_3_out);
  or or_11 (or_11_out, and_60_out, and_28_out, and_36_out, or_4_out);
  or or_12 (or_12_out, and_69_out, and_29_out, and_37_out, or_6_out);
  or or_13 (or_13_out, and_56_out, and_64_out, and_72_out, and_80_out);
  or or_14 (out_13, and_17_out, or_5_out);
  or or_15 (out_14, and_18_out, or_9_out);
  or or_16 (out_15, and_19_out, or_10_out);
  or or_17 (out_16, and_20_out, or_11_out);
  or or_18 (or_18_out, and_30_out, and_38_out, and_46_out, or_7_out);
  or or_19 (or_19_out, and_31_out, and_39_out, and_47_out, or_8_out);
  or or_20 (or_20_out, and_32_out, and_40_out, and_48_out, or_13_out);
  or or_21 (out_17, and_21_out, or_12_out);
  or or_22 (out_18, and_22_out, or_18_out);
  or or_23 (out_19, and_23_out, or_19_out);
  or or_24 (out_20, and_24_out, or_20_out);

  // Notes on the sheet:
  //   REG ADDRESS SEL
  //   DATA IN
  //   CLOCK
  //   R0
  //   R1
  //   R2
  //   R3
  //   R4
  //   R5
  //   R6
  //   R7
endmodule
